// Logisim project dec.circ as structural Verilog
module dec_2to4 (
  input  a0,
  input  a1,
  output y0,
  output y1,
  output y3,
  output y4
);

  wire not_1_out, not_2_out;

  not not_1 (not_1_out, a0);
  not not_2 (not_2_out, a1);
  and and_1 (y0, not_1_out, not_2_out);
  and and_2 (y1, a0, not_2_out);
  and and_3 (y3, a1, not_1_out);
  and and_4 (y4, a0, a1);

  // Notes on the sheet:
  //   2-4译码器
endmodule

module dec_3to8 (
  input  in_1,
  input  in_2,
  input  in_3,
  output out_4,
  output out_5,
  output out_6,
  output out_7,
  output out_8,
  output out_9,
  output out_10,
  output out_11
);

  wire [3:3] not_1_out;
  wire [7:0] dec_2to4_1_y0;

  dec_2to4 dec_2to4_1 (
    .a0(in_1), .a1(in_2), .y0(dec_2to4_1_y0[0]), .y1(dec_2to4_1_y0[1]), .y3(dec_2to4_1_y0[2]),
    .y4(dec_2to4_1_y0[3]));
  dec_2to4 dec_2to4_2 (
    .a0(in_1), .a1(in_2), .y0(dec_2to4_1_y0[4]), .y1(dec_2to4_1_y0[5]), .y3(dec_2to4_1_y0[6]),
    .y4(dec_2to4_1_y0[7]));
  not not_1 (not_1_out[3], in_3);
  assign {out_11, out_10, out_9, out_8, out_7, out_6, out_5, out_4} = dec_2to4_1_y0 & {{4{in_3}}, {4{not_1_out[3]}}};  // AND_Gate and_1, 8 bits wide
endmodule

module dec_4to16 (
  input  in_1,
  input  in_2,
  input  in_3,
  input  in_4,
  output out_5,
  output out_6,
  output out_7,
  output out_8,
  output out_9,
  output out_10,
  output out_11,
  output out_12,
  output out_13,
  output out_14,
  output out_15,
  output out_16,
  output out_17,
  output out_18,
  output out_19,
  output out_20
);

  wire [7:7] not_1_out;
  wire [15:0] dec_3to8_1_out_4;

  not not_1 (not_1_out[7], in_4);
  dec_3to8 dec_3to8_1 (
    .in_1(in_1), .in_2(in_2), .in_3(in_3), .out_4(dec_3to8_1_out_4[0]), .out_5(dec_3to8_1_out_4[1]),
    .out_6(dec_3to8_1_out_4[2]), .out_7(dec_3to8_1_out_4[3]), .out_8(dec_3to8_1_out_4[4]),
    .out_9(dec_3to8_1_out_4[5]), .out_10(dec_3to8_1_out_4[6]), .out_11(dec_3to8_1_out_4[7]));
  dec_3to8 dec_3to8_2 (
    .in_1(in_1), .in_2(in_2), .in_3(in_3), .out_4(dec_3to8_1_out_4[8]), .out_5(dec_3to8_1_out_4[9]),
    .out_6(dec_3to8_1_out_4[10]), .out_7(dec_3to8_1_out_4[11]), .out_8(dec_3to8_1_out_4[12]),
    .out_9(dec_3to8_1_out_4[13]), .out_10(dec_3to8_1_out_4[14]), .out_11(dec_3to8_1_out_4[15]));
  assign {out_20, out_19, out_18, out_17, out_16, out_15, out_14, out_13, out_12, out_11, out_10, out_9, out_8, out_7, out_6, out_5} = dec_3to8_1_out_4 & {{8{in_4}}, {8{not_1_out[7]}}};  // AND_Gate and_1, 16 bits wide
endmodule

module trans_7 (
);

  wire dec_4to16_1_out_5, dec_4to16_1_out_6, dec_4to16_1_out_7, dec_4to16_1_out_8, dec_4to16_1_out_9,
       dec_4to16_1_out_10, dec_4to16_1_out_11, dec_4to16_1_out_12, dec_4to16_1_out_13, dec_4to16_1_out_14,
       dec_4to16_1_out_15, dec_4to16_1_out_16, dec_4to16_1_out_17, dec_4to16_1_out_18, dec_4to16_1_out_19,
       dec_4to16_1_out_20, dipswitch_1_p1, dipswitch_1_p2, dipswitch_1_p3, dipswitch_1_p4, or_1_out,
       or_2_out, or_3_out, or_4_out, or_5_out, or_6_out, or_7_out, or_8_out;

  // DipSwitch dipswitch_1: pin names not known; wires that end beside it: dipswitch_1_p1, dipswitch_1_p2, dipswitch_1_p3, dipswitch_1_p4
  dec_4to16 dec_4to16_1 (
    .in_1(dipswitch_1_p1), .in_2(dipswitch_1_p2), .in_3(dipswitch_1_p3), .in_4(dipswitch_1_p4),
    .out_5(dec_4to16_1_out_5), .out_6(dec_4to16_1_out_6), .out_7(dec_4to16_1_out_7),
    .out_8(dec_4to16_1_out_8), .out_9(dec_4to16_1_out_9), .out_10(dec_4to16_1_out_10),
    .out_11(dec_4to16_1_out_11), .out_12(dec_4to16_1_out_12), .out_13(dec_4to16_1_out_13),
    .out_14(dec_4to16_1_out_14), .out_15(dec_4to16_1_out_15), .out_16(dec_4to16_1_out_16),
    .out_17(dec_4to16_1_out_17), .out_18(dec_4to16_1_out_18), .out_19(dec_4to16_1_out_19),
    .out_20(dec_4to16_1_out_20));
  or or_1 (or_1_out, dec_4to16_1_out_5, dec_4to16_1_out_14, dec_4to16_1_out_10, dec_4to16_1_out_11, dec_4to16_1_out_9, dec_4to16_1_out_13);
  or or_2 (or_2_out, dec_4to16_1_out_6, dec_4to16_1_out_7, dec_4to16_1_out_8, dec_4to16_1_out_5, dec_4to16_1_out_9, dec_4to16_1_out_12, dec_4to16_1_out_13, dec_4to16_1_out_14);
  or or_3 (or_3_out, dec_4to16_1_out_7, dec_4to16_1_out_8, dec_4to16_1_out_9, dec_4to16_1_out_14, dec_4to16_1_out_10, dec_4to16_1_out_11, dec_4to16_1_out_13);
  or or_4 (or_4_out, dec_4to16_1_out_5, dec_4to16_1_out_7, dec_4to16_1_out_8, dec_4to16_1_out_14, dec_4to16_1_out_10, dec_4to16_1_out_11, dec_4to16_1_out_13);
  or or_5 (or_5_out, dec_4to16_1_out_5, dec_4to16_1_out_6, dec_4to16_1_out_8, dec_4to16_1_out_10, dec_4to16_1_out_9, dec_4to16_1_out_11, dec_4to16_1_out_12, dec_4to16_1_out_13, dec_4to16_1_out_14);
  or or_6 (or_6_out, dec_4to16_1_out_15, dec_4to16_1_out_16, dec_4to16_1_out_17, dec_4to16_1_out_18, dec_4to16_1_out_19, dec_4to16_1_out_20);
  or or_7 (or_7_out, dec_4to16_1_out_7, dec_4to16_1_out_5, dec_4to16_1_out_11, dec_4to16_1_out_13);
  or or_8 (or_8_out, dec_4to16_1_out_5, dec_4to16_1_out_7, dec_4to16_1_out_8, dec_4to16_1_out_10, dec_4to16_1_out_11, dec_4to16_1_out_12, dec_4to16_1_out_13, dec_4to16_1_out_14);
  _7_Segment_Display u_7_segment_display_1 (
    .g(or_3_out), .f(or_1_out), .a(or_8_out), .b(or_2_out), .e(or_7_out), .d(or_4_out), .c(or_5_out),
    .dp(or_6_out));
endmodule

module trans_16 (
);

  wire [3:0] dipswitch_1_p1;

  // DipSwitch dipswitch_1: pin names not known; wires that end beside it: dipswitch_1_p1[0], dipswitch_1_p1[1], dipswitch_1_p1[2], dipswitch_1_p1[3]
  Hex_Digit_Display hex_digit_display_1 (.value(dipswitch_1_p1));  // open: dp
endmodule

module encoder_16to4 (
);

  wire dipswitch_1_p1, dipswitch_1_p2, dipswitch_1_p3, dipswitch_1_p4, dipswitch_1_p5, dipswitch_1_p6,
       dipswitch_1_p7, dipswitch_2_p1, dipswitch_2_p2, dipswitch_2_p3, dipswitch_2_p4, dipswitch_2_p5,
       dipswitch_2_p6, dipswitch_2_p7, dipswitch_2_p8;
  wire [3:0] or_1_out;

  // DipSwitch dipswitch_1: pin names not known; wires that end beside it: dipswitch_1_p1, dipswitch_1_p2, dipswitch_1_p3, dipswitch_1_p4, dipswitch_1_p5, dipswitch_1_p6, dipswitch_1_p7
  // DipSwitch dipswitch_2: pin names not known; wires that end beside it: dipswitch_2_p1, dipswitch_2_p2, dipswitch_2_p3, dipswitch_2_p4, dipswitch_2_p5, dipswitch_2_p6, dipswitch_2_p7, dipswitch_2_p8
  or or_1 (or_1_out[0], dipswitch_1_p1, dipswitch_1_p3, dipswitch_1_p5, dipswitch_1_p7, dipswitch_2_p2, dipswitch_2_p4, dipswitch_2_p6, dipswitch_2_p8);
  or or_2 (or_1_out[1], dipswitch_1_p2, dipswitch_1_p3, dipswitch_1_p6, dipswitch_1_p7, dipswitch_2_p3, dipswitch_2_p4, dipswitch_2_p7, dipswitch_2_p8);
  or or_3 (or_1_out[2], dipswitch_1_p4, dipswitch_1_p5, dipswitch_1_p6, dipswitch_1_p7, dipswitch_2_p5, dipswitch_2_p6, dipswitch_2_p7, dipswitch_2_p8);
  or or_4 (or_1_out[3], dipswitch_2_p1, dipswitch_2_p2, dipswitch_2_p3, dipswitch_2_p4, dipswitch_2_p5, dipswitch_2_p6, dipswitch_2_p7, dipswitch_2_p8);
  Hex_Digit_Display hex_digit_display_1 (.value(or_1_out));  // open: dp
endmodule

module pri_enco_4to2 (
  input  a0,
  input  a1,
  input  a2,
  input  a3,
  output y0,
  output y1
);

  wire nor_1_out, not_1_out;

  not not_1 (not_1_out, a1);
  nor nor_1 (nor_1_out, not_1_out, a2);
  or or_1 (y1, a2, a3);
  or or_2 (y0, nor_1_out, a3);

  // Notes on the sheet:
  //   2+6+8*2=24
endmodule

module pri_enco_16to4 (
);

  wire dipswitch_1_p1, dipswitch_1_p2, dipswitch_1_p3, dipswitch_1_p4, dipswitch_1_p5, dipswitch_1_p6,
       dipswitch_1_p7, dipswitch_1_p8, dipswitch_2_p1, dipswitch_2_p2, dipswitch_2_p3, dipswitch_2_p4,
       dipswitch_2_p5, dipswitch_2_p6, dipswitch_2_p7, dipswitch_2_p8;
  wire [1:0] or_4_out;
  wire [3:0] and_2_out, or_3_out;
  wire [3:1] not_2_out;
  wire [7:0] and_1_out, pri_enco_4to2_1_y0;
  wire [7:3] not_1_out;

  // DipSwitch dipswitch_1: pin names not known; wires that end beside it: dipswitch_1_p1, dipswitch_1_p2, dipswitch_1_p3, dipswitch_1_p4, dipswitch_1_p5, dipswitch_1_p6, dipswitch_1_p7, dipswitch_1_p8
  // DipSwitch dipswitch_2: pin names not known; wires that end beside it: dipswitch_2_p1, dipswitch_2_p2, dipswitch_2_p3, dipswitch_2_p4, dipswitch_2_p5, dipswitch_2_p6, dipswitch_2_p7, dipswitch_2_p8
  pri_enco_4to2 pri_enco_4to2_1 (
    .a0(dipswitch_1_p1), .a1(dipswitch_1_p2), .a2(dipswitch_1_p3), .a3(dipswitch_1_p4),
    .y0(pri_enco_4to2_1_y0[0]), .y1(pri_enco_4to2_1_y0[1]));
  pri_enco_4to2 pri_enco_4to2_2 (
    .a1(dipswitch_1_p6), .a2(dipswitch_1_p7), .a3(dipswitch_1_p8), .y0(pri_enco_4to2_1_y0[2]),
    .y1(pri_enco_4to2_1_y0[3]));  // open: a0
  pri_enco_4to2 pri_enco_4to2_3 (
    .a1(dipswitch_2_p2), .a2(dipswitch_2_p3), .a3(dipswitch_2_p4), .y0(pri_enco_4to2_1_y0[4]),
    .y1(pri_enco_4to2_1_y0[5]));  // open: a0
  pri_enco_4to2 pri_enco_4to2_4 (
    .a1(dipswitch_2_p6), .a2(dipswitch_2_p7), .a3(dipswitch_2_p8), .y0(pri_enco_4to2_1_y0[6]),
    .y1(pri_enco_4to2_1_y0[7]));  // open: a0
  or or_1 (not_2_out[3], dipswitch_1_p5, pri_enco_4to2_1_y0[2], pri_enco_4to2_1_y0[3], dipswitch_2_p5, pri_enco_4to2_1_y0[6], pri_enco_4to2_1_y0[7]);
  or or_2 (not_1_out[7], dipswitch_2_p1, pri_enco_4to2_1_y0[4], pri_enco_4to2_1_y0[5], dipswitch_2_p5, pri_enco_4to2_1_y0[6], pri_enco_4to2_1_y0[7]);
  not not_1 (not_1_out[3], not_1_out[7]);
  not not_2 (not_2_out[1], not_2_out[3]);
  assign and_1_out = {{4{not_1_out[7]}}, {4{not_1_out[3]}}} & pri_enco_4to2_1_y0;  // AND_Gate and_1, 8 bits wide
  assign or_3_out = and_1_out[3:0] | and_1_out[7:4];  // OR_Gate or_3, 4 bits wide
  assign and_2_out = or_3_out & {{2{not_2_out[3]}}, {2{not_2_out[1]}}};  // AND_Gate and_2, 4 bits wide
  assign or_4_out = and_2_out[1:0] | and_2_out[3:2];  // OR_Gate or_4, 2 bits wide
  Hex_Digit_Display hex_digit_display_1 (.value({not_1_out[7], not_2_out[3], or_4_out}));  // open: dp
endmodule

module mux_2to1 (
  input  D0,
  input  S,
  input  D1,
  output out_4
);

  wire and_1_out, and_2_out, not_1_out;

  not not_1 (not_1_out, S);
  and and_1 (and_1_out, D0, not_1_out);
  and and_2 (and_2_out, S, D1);
  or or_1 (out_4, and_1_out, and_2_out);
endmodule

module mux4_3bit (
  input  in_1,
  input  in_2,
  input  in_3,
  input  in_4,
  input  in_5,
  input  in_6,
  input  in_7,
  input  in_8,
  input  in_9,
  input  in_10,
  input  in_11,
  input  in_12,
  input  in_13,
  input  in_14,
  output out_15,
  output out_16,
  output out_17
);

  wire and_1_out, and_2_out, and_3_out, and_4_out, and_5_out, and_6_out, and_7_out, and_8_out, and_9_out,
       and_10_out, and_11_out, and_12_out, dec_2to4_1_y0, dec_2to4_1_y1, dec_2to4_1_y3, dec_2to4_1_y4;

  dec_2to4 dec_2to4_1 (
    .a0(in_7), .a1(in_8), .y0(dec_2to4_1_y0), .y1(dec_2to4_1_y1), .y3(dec_2to4_1_y3), .y4(dec_2to4_1_y4));
  and and_1 (and_1_out, in_9, dec_2to4_1_y3);
  and and_2 (and_2_out, in_10, dec_2to4_1_y3);
  and and_3 (and_3_out, in_11, dec_2to4_1_y3);
  and and_4 (and_4_out, in_12, dec_2to4_1_y4);
  and and_5 (and_5_out, in_13, dec_2to4_1_y4);
  and and_6 (and_6_out, in_14, dec_2to4_1_y4);
  and and_7 (and_7_out, in_1, dec_2to4_1_y0);
  and and_8 (and_8_out, in_2, dec_2to4_1_y0);
  and and_9 (and_9_out, in_3, dec_2to4_1_y0);
  and and_10 (and_10_out, in_4, dec_2to4_1_y1);
  and and_11 (and_11_out, in_5, dec_2to4_1_y1);
  and and_12 (and_12_out, in_6, dec_2to4_1_y1);
  or or_1 (out_15, and_7_out, and_10_out, and_1_out, and_4_out);
  or or_2 (out_16, and_8_out, and_11_out, and_2_out, and_5_out);
  or or_3 (out_17, and_9_out, and_12_out, and_3_out, and_6_out);
endmodule

module seg7_dec_hex_switch (
);

  wire and_1_out, and_2_out, and_3_out, dipswitch_4_p1, dipswitch_5_p1;
  wire [3:0] dipswitch_1_p1;

  // DipSwitch #(.number(1)) dipswitch_1: pin names not known; wires that end beside it: dipswitch_1_p1[0]
  // DipSwitch #(.number(1)) dipswitch_2: pin names not known; wires that end beside it: dipswitch_1_p1[1]
  // DipSwitch #(.number(1)) dipswitch_3: pin names not known; wires that end beside it: dipswitch_1_p1[2]
  // DipSwitch #(.number(1)) dipswitch_4: pin names not known; wires that end beside it: dipswitch_4_p1
  // DipSwitch #(.number(1)) dipswitch_5: pin names not known; wires that end beside it: dipswitch_5_p1
  and and_1 (and_1_out, dipswitch_1_p1[0], ~dipswitch_1_p1[1], ~dipswitch_1_p1[2], dipswitch_4_p1);  // AND_Gate
  and and_2 (and_2_out, ~dipswitch_1_p1[0], ~dipswitch_1_p1[1], ~dipswitch_1_p1[2], dipswitch_4_p1);  // AND_Gate
  and and_3 (and_3_out, dipswitch_4_p1, dipswitch_5_p1);
  or or_1 (dipswitch_1_p1[3], and_1_out, and_2_out, and_3_out);
  Hex_Digit_Display hex_digit_display_1 (.value(dipswitch_1_p1));  // open: dp
endmodule
